# Fritzing sketch reciver (saved by Fritzing 0.9.3b)
breadboards: 1

parts:
  Part9 = NRF24L01+ Breakout Board
  KY-2 = Keyes Relay [package=THT]
  U1 = LM2596 step down module
  Part8 = Arduino Pro Mini v13
  LED1 = smd LED [color="Red (633nm)" package="0603 [SMD]"]  # not connected
  R1 = Resistor [tolerance=±5% resistance=220 package=THT]

nets:
  GND: Part9.GND, KY-2.ground, U1.IN-, U1.OUT-, Part8.GND, R1.Pin_0
  VCC: Part9.VCC, U1.OUT+, Part8.VCC
  N1: Part9.CE, Part8.D9_PWM
  N2: Part9.CS, Part8.D10_PWM/SS
  N3: Part9.SCK, Part8.D13/SCK
  N4: Part9.MOSI, Part8.D11_PWM/MOSI
  N5: Part9.MISO, Part8.D12/MISO
  N6: KY-2.signal, Part8.D2
  N7: KY-2.power, U1.IN+

custom parts:
  Keyes Relay: The Keyes 5V relay module is suitable for SCM development, home appliance control. It uses a 5V~12V TIL control signal which can control DC / AC signal.
  LM2596 step down module: LM2596 DC-DC step down power supply module 3 A.
