# Fritzing sketch transmiter (saved by Fritzing 0.9.3b)
breadboards: 1

parts:
  Part2 = Arduino Uno (Rev3) - ICSP
  Part5 = NRF24L01+ Breakout Board
  Part6 = LCD1602-I2C
  Part7 = Adafruit BMP280 [part_number="Adafruit #2651"]
  S1 = Pushbutton [package="[SMD]"]
  S2 = Pushbutton [package="[SMD]"]
  R1 = Resistor [tolerance=±5% resistance=220 package=THT]
  R2 = Resistor [tolerance=±5% resistance=220 package=THT]
  BB1 = 4-Line Bi-Directional Level Shifter

nets:
  N1: Part2.ICSP_MISO, Part2.D12/MISO, Part5.MISO
  N2: Part2.D11_PWM/MOSI, Part5.MOSI
  N3: Part2.D13/SCK, Part5.SCK
  GND: Part2.GND, Part5.GND, Part6.GND, Part7.GND, S1.Pin_1, S1.Pin_2, S2.Pin_1, S2.Pin_2, BB1.GND
  N4: Part2.A4/SDA, Part6.SDA, BB1.B2
  N5: Part2.A5/SCL, Part6.SCL, BB1.B1
  N6: Part2.D2, Part5.CE
  N7: Part2.D3_PWM, Part5.CS
  N8: Part2.D6_PWM, S2.Pin_3, S2.Pin_4, R1.Pin_1
  N9: Part2.D7, S1.Pin_3, S1.Pin_4, R2.Pin_1
  3V3: Part2.3V3, Part5.VCC, Part7.3.3V, BB1.LV
  5V: Part2.5V, Part6.VCC, R1.Pin_0, R2.Pin_0, BB1.HV
  N10: Part7.SCK/SCL, BB1.A1
  N11: Part7.SDI/SDA, BB1.A2

custom parts:
  LCD1602-I2C: A standard character display, usually with 2x16 characters. Comes in many colors with LCM1602 IIC attached.
  Adafruit BMP280: Bosch has stepped up their game with their new BMP280 sensor, an environmental sensor with temperature, barometric pressure that is the next generation upgrade to the BMP085/BMP180/BMP183. This sensor is great for all sorts of weather sensing and can even be used in both I2C and SPI! This precision sensor from Bosch is the best low-cost, precision sensing solution for measuring barometric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
  4-Line Bi-Directional Level Shifter: 4-Channel Bi-Directional Level Shifter
